// Logisim project shift.circ as structural Verilog: 1 circuit, main circuit main
module main (
  input  [1:0] Operation,
  input  B_in,
  output A7,
  output A6,
  output A5,
  output A4,
  output A3,
  output A2,
  output A1,
  output A0,
  output B_out
);

  wire and_1_out, Clock_out, decoder_1_out1, decoder_1_out2, decoder_2_out3, multiplexer_1_out,
       multiplexer_2_out, multiplexer_3_out, multiplexer_4_out, multiplexer_5_out, multiplexer_6_out,
       multiplexer_7_out, multiplexer_8_out, multiplexer_9_out;

  Clock Clock (.out(Clock_out));
  D_Flip_Flop d_ff_1 (.D(multiplexer_1_out), .clk(Clock_out), .Q(B_out));  // open: Qn, preset, reset
  Multiplexer #(.select(2), .enable("false")) multiplexer_1 (
    .in1(A0), .in2(A7), .out(multiplexer_1_out), .sel(Operation));  // open: in0, in3
  D_Flip_Flop d_ff_2 (.D(multiplexer_2_out), .clk(Clock_out), .Q(A7));  // open: Qn, preset, reset
  Multiplexer #(.select(2), .enable("false")) multiplexer_2 (
    .in0(A7), .in1(decoder_1_out1), .in2(A6), .in3(and_1_out), .out(multiplexer_2_out), .sel(Operation));
  D_Flip_Flop d_ff_3 (.D(multiplexer_3_out), .clk(Clock_out), .Q(A6));  // open: Qn, preset, reset
  Multiplexer #(.select(2), .enable("false")) multiplexer_3 (
    .in0(A6), .in1(A7), .in2(A5), .in3(A7), .out(multiplexer_3_out), .sel(Operation));
  D_Flip_Flop d_ff_4 (.D(multiplexer_4_out), .clk(Clock_out), .Q(A5));  // open: Qn, preset, reset
  Multiplexer #(.select(2), .enable("false")) multiplexer_4 (
    .in0(A5), .in1(A6), .in2(A4), .in3(A6), .out(multiplexer_4_out), .sel(Operation));
  D_Flip_Flop d_ff_5 (.D(multiplexer_5_out), .clk(Clock_out), .Q(A4));  // open: Qn, preset, reset
  Multiplexer #(.select(2), .enable("false")) multiplexer_5 (
    .in0(A4), .in1(A5), .in2(A3), .in3(A5), .out(multiplexer_5_out), .sel(Operation));
  Decoder #(.select(2)) decoder_1 (
    .out1(decoder_1_out1), .out2(decoder_1_out2), .sel(Operation), .en(B_in));  // open: out0, out3
  D_Flip_Flop d_ff_6 (.D(multiplexer_6_out), .clk(Clock_out), .Q(A3));  // open: Qn, preset, reset
  Multiplexer #(.select(2), .enable("false")) multiplexer_6 (
    .in0(A3), .in1(A4), .in2(A2), .in3(A4), .out(multiplexer_6_out), .sel(Operation));
  D_Flip_Flop d_ff_7 (.D(multiplexer_7_out), .clk(Clock_out), .Q(A2));  // open: Qn, preset, reset
  Multiplexer #(.select(2), .enable("false")) multiplexer_7 (
    .in0(A2), .in1(A3), .in2(A1), .in3(A3), .out(multiplexer_7_out), .sel(Operation));
  D_Flip_Flop d_ff_8 (.D(multiplexer_8_out), .clk(Clock_out), .Q(A1));  // open: Qn, preset, reset
  Multiplexer #(.select(2), .enable("false")) multiplexer_8 (
    .in0(A1), .in1(A2), .in2(A0), .in3(A2), .out(multiplexer_8_out), .sel(Operation));
  D_Flip_Flop d_ff_9 (.D(multiplexer_9_out), .clk(Clock_out), .Q(A0));  // open: Qn, preset, reset
  Multiplexer #(.select(2), .enable("false")) multiplexer_9 (
    .in0(A0), .in1(A1), .in2(decoder_1_out2), .in3(A1), .out(multiplexer_9_out), .sel(Operation));
  Decoder #(.select(2)) decoder_2 (.out3(decoder_2_out3), .sel(Operation));  // open: out0, out1, out2, en
  and and_1 (and_1_out, A0, decoder_2_out3);
endmodule
